# Fritzing sketch photoresistor_V2 (saved by Fritzing 0.8.7b)
circuit board: 8.34199cm x 9.41636cm

parts:
  LED1 = LED - 5mm [color="Red (633nm)" package="5 mm [THT]"]
  LED2 = LED - 5mm [color="Red (633nm)" package="5 mm [THT]"]
  LED3 = LED - 5mm [color="Red (633nm)" package="5 mm [THT]"]
  Part1 = Arduino Uno (Rev3)
  R1 = Photocell (LDR) [package=THT]
  VCC1 = Battery block 9V
  R2 = Resistor [tolerance=±5% resistance=10k package=THT]
  R2_2 = Resistor [tolerance=±5% resistance=10k package="1206 [SMD]"]

nets:
  N1: LED1.cathode, LED2.cathode, LED3.cathode, Part1.GND, R1.pin_0, VCC1.-
  N2: LED1.anode, Part1.D12/MISO
  N3: LED2.anode, Part1.D11_PWM/MOSI
  N4: LED3.anode, Part1.D10_PWM/SS
  N5: Part1.A0, R1.pin_1, R2.Pin_1, R2_2.Pin_1
  N6: Part1.5V, R2.Pin_0, R2_2.Pin_0
  N7: Part1.VIN, VCC1.+
