# Fritzing sketch Pulse ox and lcd (saved by Fritzing 0.8.7b)
circuit board: 8.976cm x 6.98722cm

parts:
  Part1 = Arduino Uno (Rev3)
  U1 = LCD-16X2 [package=lcd-16x2]
  LED1 = LED - 5mm [color="Red (633nm)" package="5 mm [THT]"]
  LED2 = LED - 5mm [color="Red (633nm)" package="5 mm [THT]"]
  JACK1 = 2.1mm Barrel Jack with Terminal Block
  VCC1 = Battery block 9V
  U2 = DCM01 Reflective Blood Sensor [package=dcm01]

nets:
  N1: Part1.A0, U2.3
  N2: Part1.D8, U1.E, U1.DB0
  N3: Part1.D9_PWM, U1.DB4
  N4: Part1.D10_PWM/SS, U1.DB5
  N5: Part1.D11_PWM/MOSI, U1.DB6
  N6: Part1.D12/MISO, U1.DB7, U1.A
  N7: Part1.D13/SCK, LED1.cathode
  GND: Part1.GND, U1.VSS, LED1.anode, LED2.anode, U2.1
  N8: Part1.AREF, Part1.3V3, U2.2
  N9: Part1.D5_PWM, LED2.cathode
  N10: Part1.D6_PWM, U1.RS
  N11: Part1.D7, U1.R_W
  5V: Part1.5V, U1.VDD, U1.VO
  N12: JACK1.POS, VCC1.+
  N13: JACK1.NEG, VCC1.-

notes:
  Pulse Ox Sensor
